// Digital circuit ExamenII_Orga.dig as structural Verilog
module ExamenII_Orga (
  input  [31:0] addr,
  output [31:0] data,
  output hit
);

  wire comparator_1_eq, valid;
  wire [51:32] CacheMem_d;

  ROM #(.AddrBits(10), .Bits(53)) CacheMem (.A(addr[11:2]), .sel(1'b1), .D({valid, CacheMem_d, data}));
  and and_1 (hit, valid, comparator_1_eq);
  Comparator #(.Bits(20)) comparator_1 (.a(CacheMem_d), .b(addr[31:12]), .eq(comparator_1_eq));  // open: gt, lt

  // Other names for the same wires on the sheet: byte_offset[1:0] = addr[1:0]; index[9:0] = addr[11:2];
  //   tag[19:0] = addr[31:12]
endmodule
